// Logisim project Arilla.circ as structural Verilog
module ALU (
  input  [31:0] A,
  input  [31:0] B,
  input  [3:0] op,
  output [31:0] C,
  output zero
);

  wire comparator_1_lt, comparator_2_lt;
  wire [31:0] adder_1_out, and_1_out, bit_extender_1_out, bit_extender_2_out, not_1_out, not_2_out,
       not_3_out, or_1_out, shifter_1_out, shifter_2_out, shifter_3_out, subtractor_1_out, xor_1_out;

  Adder #(.width(32)) adder_1 (.a(A), .b(B), .out(adder_1_out));  // open: cin, cout
  Subtractor #(.width(32)) subtractor_1 (.a(A), .b(B), .out(subtractor_1_out));  // open: bin, bout
  Shifter #(.width(32)) shifter_1 (.in(A), .\dist (B[4:0]), .out(shifter_1_out));
  assign bit_extender_1_out = {{31{1'b0}}, comparator_1_lt};  // Bit_Extender bit_extender_1
  Comparator #(.width(32)) comparator_1 (.a(A), .b(B), .lt(comparator_1_lt));  // open: gt, eq
  assign bit_extender_2_out = {{31{1'b0}}, comparator_2_lt};  // Bit_Extender bit_extender_2
  Comparator #(.mode("unsigned"), .width(32)) comparator_2 (.a(A), .b(B), .lt(comparator_2_lt));  // open: gt, eq
  assign xor_1_out = A ^ B;  // XOR_Gate xor_1, 32 bits wide
  Shifter #(.shift("lr"), .width(32)) shifter_2 (.in(A), .\dist (B[4:0]), .out(shifter_2_out));
  assign or_1_out = A | B;  // OR_Gate or_1, 32 bits wide
  assign and_1_out = A & B;  // AND_Gate and_1, 32 bits wide
  Shifter #(.shift("ar"), .width(32)) shifter_3 (.in(A), .\dist (B[4:0]), .out(shifter_3_out));
  assign not_1_out = ~subtractor_1_out;  // NOT_Gate not_1, 32 bits wide
  assign not_2_out = ~bit_extender_1_out;  // NOT_Gate not_2, 32 bits wide
  assign not_3_out = ~bit_extender_2_out;  // NOT_Gate not_3, 32 bits wide
  Multiplexer #(.enable("false"), .select(4), .width(32)) multiplexer_1 (
    .in0(adder_1_out), .in1(shifter_1_out), .in2(bit_extender_1_out), .in3(bit_extender_2_out),
    .in4(xor_1_out), .in5(shifter_2_out), .in6(or_1_out), .in7(and_1_out), .in8(subtractor_1_out),
    .in9(not_1_out), .in10(not_2_out), .in11(bit_extender_2_out), .in12(bit_extender_1_out),
    .in13(shifter_3_out), .in14(not_3_out), .in15(subtractor_1_out), .out(C), .sel(op));
  Comparator #(.mode("unsigned"), .width(32)) comparator_3 (.a(C), .b({32{1'b0}}), .eq(zero));  // open: gt, lt
endmodule

module RegFile (
  input  clk,
  input  [31:0] data,
  input  rst,
  input  [4:0] s1,
  input  wr,
  input  [4:0] d,
  input  [4:0] s2,
  output exception,
  output [31:0] rs1,
  output [31:0] rs2
);

  wire decoder_1_out1, decoder_1_out2, decoder_1_out3, decoder_1_out4, decoder_1_out5, decoder_1_out6,
       decoder_1_out7;
  wire [31:0] R1_q, register_1_q, register_2_q, register_3_q, register_4_q, register_5_q, register_6_q,
       register_7_q, register_8_q, register_9_q, register_10_q, register_11_q, register_12_q, register_13_q,
       register_14_q;

  Decoder #(.select(5)) decoder_1 (
    .out0(exception), .out1(decoder_1_out1), .out2(decoder_1_out2), .out3(decoder_1_out3),
    .out4(decoder_1_out4), .out5(decoder_1_out5), .out6(decoder_1_out6), .out7(decoder_1_out7), .sel(d),
    .en(wr));  // open: out8, out9, out10, out11, out12, out13, out14, out15, out16, out17, out18, out19, out20, out21, out22, out23, out24, out25, out26, out27, out28, out29, out30, out31
  Register #(.width(32)) R1 (.D(data), .en(decoder_1_out1), .clk(clk), .Q(R1_q), .clr(rst));
  Register #(.width(32)) register_1 (.D(data), .en(decoder_1_out2), .clk(clk), .Q(register_1_q), .clr(rst));
  Register #(.width(32)) register_2 (.D(data), .en(decoder_1_out3), .clk(clk), .Q(register_2_q), .clr(rst));
  Register #(.width(32)) register_3 (.D(data), .en(decoder_1_out4), .clk(clk), .Q(register_3_q), .clr(rst));
  Register #(.width(32)) register_4 (.D(data), .en(decoder_1_out5), .clk(clk), .Q(register_4_q), .clr(rst));
  Register #(.width(32)) register_5 (.D(data), .en(decoder_1_out6), .clk(clk), .Q(register_5_q), .clr(rst));
  Register #(.width(32)) register_6 (.D(data), .en(decoder_1_out7), .clk(clk), .Q(register_6_q), .clr(rst));
  Register #(.width(32)) register_7 (.D(data), .clk(clk), .Q(register_7_q), .clr(rst));  // open: en
  Register #(.width(32)) register_8 (.D(data), .clk(clk), .Q(register_8_q), .clr(rst));  // open: en
  Register #(.width(32)) register_9 (.D(data), .clk(clk), .Q(register_9_q), .clr(rst));  // open: en
  Register #(.width(32)) register_10 (.D(data), .clk(clk), .Q(register_10_q), .clr(rst));  // open: en
  Register #(.width(32)) register_11 (.D(data), .clk(clk), .Q(register_11_q), .clr(rst));  // open: en
  Register #(.width(32)) register_12 (.D(data), .clk(clk), .Q(register_12_q), .clr(rst));  // open: en
  Register #(.width(32)) register_13 (.D(data), .clk(clk), .Q(register_13_q), .clr(rst));  // open: en
  Register #(.width(32)) register_14 (.D(data), .clk(clk), .Q(register_14_q), .clr(rst));  // open: en
  Multiplexer #(.enable("false"), .select(5), .width(32)) multiplexer_1 (
    .in0({32{1'b0}}), .in1(R1_q), .in2(register_1_q), .in3(register_2_q), .in4(register_3_q),
    .in5(register_4_q), .out(rs1), .sel(s1));  // open: in6, in7, in8, in9, in10, in11, in12, in13, in14, in15, in16, in17, in18, in19, in20, in21, in22, in23, in24, in25, in26, in27, in28, in29, in30, in31
  Multiplexer #(.enable("false"), .select(5), .width(32)) multiplexer_2 (
    .in0({32{1'b0}}), .in1(R1_q), .in2(register_1_q), .in3(register_2_q), .in4(register_3_q),
    .in5(register_4_q), .out(rs2), .sel(s2));  // open: in6, in7, in8, in9, in10, in11, in12, in13, in14, in15, in16, in17, in18, in19, in20, in21, in22, in23, in24, in25, in26, in27, in28, in29, in30, in31
endmodule

module MDRGen (
  input  [31:0] DataIn,
  input  [2:0] function3,
  input  [31:0] Address,
  output [31:0] DataOut,
  output exception
);

  wire and_1_out, and_2_out, or_1_out;
  wire [7:0] multiplexer_1_out;
  wire [15:0] multiplexer_2_out;
  wire [31:0] bit_extender_1_out, bit_extender_2_out, bit_extender_3_out, bit_extender_4_out;

  Multiplexer #(.enable("false"), .select(2), .width(8)) multiplexer_1 (
    .in0(DataIn[7:0]), .in1(DataIn[15:8]), .in2(DataIn[23:16]), .in3(DataIn[31:24]), .out(multiplexer_1_out),
    .sel(Address[1:0]));
  Multiplexer #(.enable("false"), .width(16)) multiplexer_2 (
    .in0(DataIn[15:0]), .in1(DataIn[31:16]), .out(multiplexer_2_out), .sel(Address[1]));
  assign bit_extender_1_out = {{24{1'b0}}, multiplexer_1_out};  // Bit_Extender bit_extender_1
  assign bit_extender_2_out = {{16{1'b0}}, multiplexer_2_out};  // Bit_Extender bit_extender_2
  assign bit_extender_3_out = {{24{multiplexer_1_out[7]}}, multiplexer_1_out};  // Bit_Extender bit_extender_3
  assign bit_extender_4_out = {{16{multiplexer_2_out[15]}}, multiplexer_2_out};  // Bit_Extender bit_extender_4
  Multiplexer #(.enable("false"), .select(3), .width(32)) multiplexer_3 (
    .in0(bit_extender_3_out), .in1(bit_extender_4_out), .in2(DataIn), .in4(bit_extender_1_out),
    .in5(bit_extender_2_out), .out(DataOut), .sel(function3));  // open: in3, in6, in7
  or or_1 (or_1_out, Address[0], Address[1]);
  and and_1 (and_1_out, function3[1], or_1_out);
  and and_2 (and_2_out, function3[0], Address[0]);
  or or_2 (exception, and_1_out, and_2_out);

  // Other names for the same wires on the sheet: MDR[31:0] = DataIn
endmodule

module MultiCycleCore (
);

  wire AddrALU, ALU_PC, aluzero, and_1_out, clk, mxA0, mxA1, mxB0, mxB1, mxB2, mxDest0, mxDest1, or_1_out,
       rst, wrA, wrB, wrbrPC, wrC, wrIR, wrMDR, wrMEM, wrPC, wrReg;
  wire [2:0] function3;
  wire [4:0] destination, source1, source2, st_imm;
  wire [6:0] function7, opcode;
  wire [11:0] rbranch_imm;
  wire [12:0] multiplexer_2_out;
  wire [12:3] upper_imm;
  wire [19:0] jal_imm;
  wire [30:0] bit_extender_1_out, bit_extender_2_out;
  wire [31:0] A_q, ALUOut, B, C, MDR_q, mdrgen_1_dataout, multiplexer_1_out, multiplexer_3_out,
       multiplexer_4_out, multiplexer_5_out, PC, regfile_1_rs1, regfile_1_rs2, SRAM_dout, undriven,
       undriven_2, undriven_3;

  Button u_rst (.out(rst));
  Clock u_clk (.out(clk));
  Multiplexer #(.enable("false"), .width(32)) multiplexer_1 (
    .in0(ALUOut), .in1(C), .out(multiplexer_1_out), .sel(ALU_PC));
  or or_1 (or_1_out, wrPC, and_1_out);
  and and_1 (and_1_out, aluzero, wrbrPC);
  Register #(.width(32)) u_PC (.D(multiplexer_1_out), .en(or_1_out), .clk(clk), .Q(PC), .clr(rst));
  Multiplexer #(.enable("false"), .width(13)) multiplexer_2 (
    .in0(PC[14:2]), .in1(C[14:2]), .out(multiplexer_2_out), .sel(AddrALU));
  RAM #(.addrWidth(13), .dataWidth(32)) SRAM (
    .addr(multiplexer_2_out), .we(wrMEM), .oe(1'b1), .clk(clk), .din(B), .dout(SRAM_dout));
  Register #(.width(32)) IR (
    .D(SRAM_dout), .en(wrIR), .clk(clk), .Q({function7, upper_imm, function3, st_imm, opcode}), .clr(rst));
  Register #(.width(32)) MDR (.D(SRAM_dout), .en(wrMDR), .clk(clk), .Q(MDR_q), .clr(rst));
  MDRGen mdrgen_1 (.DataIn(MDR_q), .function3(function3), .Address(C), .DataOut(mdrgen_1_dataout));  // open: exception
  Multiplexer #(.enable("false"), .select(2), .width(32)) multiplexer_3 (
    .in0(C), .in1(mdrgen_1_dataout), .in2({function7, upper_imm, function3, {12{1'b0}}}), .in3(PC),
    .out(multiplexer_3_out), .sel({mxDest1, mxDest0}));
  OpcodeGen opcodegen_1 (.opcode(opcode));  // open: OP, OP_IMM, BRANCH, LUI, AUIPC, JAL, JALR, LOAD, STORE, exception
  RegFile regfile_1 (
    .clk(clk), .data(multiplexer_3_out), .rst(rst), .s1(source1), .wr(wrReg), .d(destination), .s2(source2),
    .rs1(regfile_1_rs1), .rs2(regfile_1_rs2));  // open: exception
  Register #(.width(32)) A (.D(regfile_1_rs1), .en(wrA), .clk(clk), .Q(A_q), .clr(rst));
  Register #(.width(32)) u_B (.D(regfile_1_rs2), .en(wrB), .clk(clk), .Q(B), .clr(rst));
  assign bit_extender_1_out = {{19{1'b0}}, rbranch_imm};  // Bit_Extender bit_extender_1
  assign bit_extender_2_out = {{11{1'b0}}, jal_imm};  // Bit_Extender bit_extender_2
  Multiplexer #(.enable("false"), .select(2), .width(32)) multiplexer_4 (
    .in0(A_q), .in1(PC), .out(multiplexer_4_out), .sel({mxA1, mxA0}));  // open: in2, in3
  Multiplexer #(.enable("false"), .select(3), .width(32)) multiplexer_5 (
    .in0(B), .in1(32'h4), .in2({bit_extender_1_out, 1'b0}),
    .in3({function7, upper_imm, function3, {12{1'b0}}}), .in4({bit_extender_2_out, 1'b0}), .in5(undriven),
    .in6(undriven_2), .in7(undriven_3), .out(multiplexer_5_out), .sel({mxB2, mxB1, mxB0}));
  ALU alu_1 (.C(ALUOut), .zero(aluzero), .A(multiplexer_4_out), .B(multiplexer_5_out));  // open: op
  Register #(.width(32)) u_C (.D(ALUOut), .en(wrC), .clk(clk), .Q(C), .clr(rst));

  // Other names for the same wires on the sheet: upper_imm (some bits) = {function7, function3};
  //   st_imm[11:5] = function7

  // Notes on the sheet:
  //   LUI
  //   LUI
  //   AUIPC
  //   JALR
  //   st_imm
  //   imm
endmodule

module OpcodeGen (
  input  [6:0] opcode,
  output OP,
  output OP_IMM,
  output BRANCH,
  output LUI,
  output AUIPC,
  output JAL,
  output JALR,
  output LOAD,
  output STORE,
  output exception
);

  Comparator #(.mode("unsigned"), .width(7)) comparator_1 (.a(opcode), .b(7'b0110011), .eq(OP));  // open: gt, lt
  Comparator #(.mode("unsigned"), .width(7)) comparator_2 (.a(opcode), .b(7'b0010011), .eq(OP_IMM));  // open: gt, lt
  Comparator #(.mode("unsigned"), .width(7)) comparator_3 (.a(opcode), .b(7'b1100011), .eq(BRANCH));  // open: gt, lt
  Comparator #(.mode("unsigned"), .width(7)) comparator_4 (.a(opcode), .b(7'b0110111), .eq(LUI));  // open: gt, lt
  Comparator #(.mode("unsigned"), .width(7)) comparator_5 (.a(opcode), .b(7'b0010111), .eq(AUIPC));  // open: gt, lt
  Comparator #(.mode("unsigned"), .width(7)) comparator_6 (.a(opcode), .b(7'b1101111), .eq(JAL));  // open: gt, lt
  Comparator #(.mode("unsigned"), .width(7)) comparator_7 (.a(opcode), .b(7'b1100111), .eq(JALR));  // open: gt, lt
  Comparator #(.mode("unsigned"), .width(7)) comparator_8 (.a(opcode), .b(7'b0000011), .eq(LOAD));  // open: gt, lt
  Comparator #(.mode("unsigned"), .width(7)) comparator_9 (.a(opcode), .b(7'b0100011), .eq(STORE));  // open: gt, lt
  nor nor_1 (exception, STORE, LOAD, JALR, JAL, AUIPC, LUI, BRANCH, OP_IMM, OP);
endmodule
